// Logisim project alu.circ as structural Verilog: 1 circuit, main circuit main
module main (
  input  [31:0] X,
  input  [31:0] Y,
  input  [3:0] Switch,
  output Signed_Overflow,
  output Equal,
  output [31:0] Result
);

  wire addres, and_2_out, and_4_out, and_6_out, and_7_out, comparator_1_lt, comparator_2_lt, comparator_4_eq,
       comparator_4_gt, comparator_4_lt, comparator_5_eq, comparator_5_gt, comparator_5_lt, comparator_6_eq,
       comparator_6_gt, comparator_6_lt, comparator_7_eq, comparator_7_gt, comparator_7_lt, comparator_8_eq,
       comparator_8_gt, comparator_8_lt, comparator_9_eq, comparator_9_gt, comparator_9_lt, or_2_out,
       or_4_out, or_5_out, overflowadd, overflowadd1, overflowresult, overflowsub1, overflowsub2,
       overflowsubresult, subres, yres;
  wire [31:0] add, addu, \and , \or , sll, slt, sltu, sra, srl, sub, subu;

  Shifter #(.width(32)) shifter_1 (.in(Y), .\dist (X[4:0]), .out(sll));
  Shifter #(.width(32), .shift("lr")) shifter_2 (.in(Y), .\dist (X[4:0]), .out(srl));
  Shifter #(.width(32), .shift("ar")) shifter_3 (.in(Y), .\dist (X[4:0]), .out(sra));
  Adder #(.width(32)) adder_1 (.a(X), .b(Y), .out(addu));  // open: cin, cout
  Subtractor #(.width(32)) subtractor_1 (.a(X), .b(Y), .out(subu));  // open: bin, bout
  assign \and  = X & Y;  // AND_Gate and_1, 32 bits wide
  assign \or  = X | Y;  // OR_Gate or_1, 32 bits wide
  Comparator #(.width(32)) comparator_1 (.a(X), .b(Y), .lt(comparator_1_lt));  // open: gt, eq
  Comparator #(.width(32), .mode("unsigned")) comparator_2 (.a(X), .b(Y), .lt(comparator_2_lt));  // open: gt, eq
  Comparator #(.width(32)) comparator_3 (.a(X), .b(Y), .eq(Equal));  // open: gt, lt
  assign slt = {{31{1'b0}}, comparator_1_lt};  // Bit_Extender bit_extender_1
  assign sltu = {{31{1'b0}}, comparator_2_lt};  // Bit_Extender bit_extender_2
  Multiplexer #(.select(4), .width(32)) multiplexer_1 (
    .in0(sll), .in1(srl), .in2(sra), .in5(add), .in6(addu), .in7(sub), .in8(subu), .in9(\and ), .in10(\or ),
    .in11(slt), .in12(sltu), .out(Result), .sel(Switch));  // open: in3, in4, in13, in14, in15, en
  Adder #(.width(32)) adder_2 (.a(X), .b(Y), .out(add));  // open: cin, cout
  Comparator #(.width(32)) comparator_4 (
    .a({32{1'b0}}), .b(X), .gt(comparator_4_gt), .eq(comparator_4_eq), .lt(comparator_4_lt));
  Comparator #(.width(32)) comparator_5 (
    .a(Y), .b({32{1'b0}}), .gt(comparator_5_gt), .eq(comparator_5_eq), .lt(comparator_5_lt));
  Comparator #(.width(32)) comparator_6 (
    .a({32{1'b0}}), .b(add), .gt(comparator_6_gt), .eq(comparator_6_eq), .lt(comparator_6_lt));
  or or_2 (or_2_out, comparator_4_eq, comparator_4_lt);
  or or_3 (addres, comparator_6_eq, comparator_6_lt);
  or or_4 (or_4_out, comparator_5_gt, comparator_5_eq);
  Subtractor #(.width(32)) subtractor_2 (.a(X), .b(Y), .out(sub));  // open: bin, bout
  and and_2 (and_2_out, or_2_out, comparator_6_gt);
  and and_3 (overflowadd, and_2_out, or_4_out);
  Comparator #(.width(32)) comparator_7 (
    .a({32{1'b0}}), .b(X), .gt(comparator_7_gt), .eq(comparator_7_eq), .lt(comparator_7_lt));
  Comparator #(.width(32)) comparator_8 (
    .a(Y), .b({32{1'b0}}), .gt(comparator_8_gt), .eq(comparator_8_eq), .lt(comparator_8_lt));
  and and_4 (and_4_out, comparator_5_lt, comparator_4_gt);
  and and_5 (overflowadd1, addres, and_4_out);
  or or_5 (or_5_out, comparator_7_eq, comparator_7_lt);
  Comparator #(.width(32)) comparator_9 (
    .a({32{1'b0}}), .b(sub), .gt(comparator_9_gt), .eq(comparator_9_eq), .lt(comparator_9_lt));
  or or_6 (subres, comparator_9_lt, comparator_9_eq);
  or or_7 (yres, comparator_8_gt, comparator_8_eq);
  and and_6 (and_6_out, or_5_out, comparator_9_gt);
  and and_7 (and_7_out, comparator_7_gt, yres);
  and and_8 (overflowsub2, and_6_out, comparator_8_lt);
  or or_8 (overflowresult, overflowadd, overflowadd1);
  Multiplexer #(.select(4)) multiplexer_2 (
    .in0(1'b0), .in1(1'b0), .in2(1'b0), .in5(overflowresult), .in6(1'b0), .in7(overflowsubresult),
    .in8(1'b0), .in9(1'b0), .in10(1'b0), .in11(1'b0), .in12(1'b0), .out(Signed_Overflow), .sel(Switch));  // open: in3, in4, in13, in14, in15, en
  and and_9 (overflowsub1, and_7_out, subres);
  or or_9 (overflowsubresult, overflowsub1, overflowsub2);

  // Other names for the same wires on the sheet: overflow = Signed_Overflow; S[3:0] = Switch

  // Notes on the sheet:
  //   INPUTS to your circuit
  //   DON'T CHANGE THE LOCATIONS OF THE INPUTS AND OUTPUTS!
  //   OUTPUTS from your circuit
endmodule
