// Logisim project cpu.circ as structural Verilog: 1 circuit, main circuit main
module main (
  input  [31:0] INSTRUCTION,
  input  CLOCK,
  output [31:0] FETCH_ADDRESS,
  output [31:0] s0_Value,
  output [31:0] s1_Value,
  output [31:0] s2_Value,
  output [31:0] ra_Value,
  output [31:0] sp_Value
);

  wire Add, Addi, Addiu, Addu, ALUSrc, And, and_13_out, and_14_out, Andi, Beq, Bne, branchSign,
       comparator_2_eq, comparator_3_eq, comparator_4_eq, comparator_5_eq, comparator_6_eq, comparator_7_eq,
       comparator_8_eq, comparator_11_eq, comparator_12_eq, comparator_13_eq, comparator_14_eq,
       comparator_15_eq, Eq, ExtOp, J, Jal, Jr, Lui_t, Lw, main_2_signed_overflow, MemWr, NopS, nPCsel, Or,
       or_6_out, or_7_out, or_9_out, or_10_out, or_12_out, or_13_out, Ori, RegDst, Rtype, Shamt, Sll, Slt,
       Slti, Sltiu, Sltu, Sra, Srl, Sub, Subu, Sw, Swinc, WriteReg;
  wire [3:0] ALUCtr, multiplexer_13_out, multiplexer_14_out, multiplexer_15_out, multiplexer_16_out,
       multiplexer_17_out, multiplexer_18_out, multiplexer_19_out, multiplexer_21_out, multiplexer_22_out;
  wire [4:0] multiplexer_3_out, multiplexer_4_out, multiplexer_5_out;
  wire [5:0] Funct, Opcode;
  wire [15:6] Imm;
  wire [25:16] Jump;
  wire [27:0] PCX;
  wire [31:0] adder_1_out, adder_2_out, bit_extender_1_out, bit_extender_2_out, bit_extender_4_out, Jreg,
       Jumper, LUI, main_1_read_data_2, main_2_result, main_3_p5, multiplexer_1_out, multiplexer_2_out,
       multiplexer_6_out, multiplexer_7_out, multiplexer_8_out, multiplexer_9_out, multiplexer_10_out,
       multiplexer_11_out, multiplexer_12_out, ShamtF, shifter_1_out, subtractor_1_out, WriteData;

  Multiplexer #(.width(32)) multiplexer_1 (
    .in0(multiplexer_8_out), .in1({Jumper[31:28], Jump, Imm, Funct, Jumper[1:0]}), .out(multiplexer_1_out),
    .sel(J));  // open: en
  Multiplexer #(.width(32)) multiplexer_2 (
    .in0(multiplexer_1_out), .in1(Jreg), .out(multiplexer_2_out), .sel(Jr));  // open: en
  Comparator #(.width(6)) comparator_1 (.a(Opcode), .b({6{1'b0}}), .eq(Rtype));  // open: gt, lt
  Register #(.width(32)) PC (.D(multiplexer_2_out), .Q(FETCH_ADDRESS), .clk(CLOCK));  // open: en, clr
  Comparator #(.width(6)) comparator_2 (.a(Funct), .b(6'b100000), .eq(comparator_2_eq));  // open: gt, lt
  Comparator #(.width(6)) comparator_3 (.a(Funct), .b(6'b000001), .eq(comparator_3_eq));  // open: gt, lt
  Comparator #(.width(6)) comparator_4 (.a(Funct), .b(6'b100100), .eq(comparator_4_eq));  // open: gt, lt
  Comparator #(.width(6)) comparator_5 (.a(Funct), .b(6'b100101), .eq(comparator_5_eq));  // open: gt, lt
  Comparator #(.width(6)) comparator_6 (.a(Funct), .b(6'b101010), .eq(comparator_6_eq));  // open: gt, lt
  Comparator #(.width(6)) comparator_7 (.a(Funct), .b(6'b101011), .eq(comparator_7_eq));  // open: gt, lt
  Comparator #(.width(6)) comparator_8 (.a(Funct), .b(6'b001000), .eq(comparator_8_eq));  // open: gt, lt
  Comparator #(.width(6)) comparator_9 (.a(Opcode), .b(6'b000010), .eq(J));  // open: gt, lt
  Comparator #(.width(6)) comparator_10 (.a(Opcode), .b(6'b000011), .eq(Jal));  // open: gt, lt
  Adder #(.width(32)) adder_1 (.a(32'h4), .b(FETCH_ADDRESS), .out(adder_1_out));  // open: cin, cout
  and and_1 (Add, Rtype, comparator_2_eq);
  and and_2 (Addu, Rtype, comparator_3_eq);
  and and_3 (And, Rtype, comparator_4_eq);
  and and_4 (Or, Rtype, comparator_5_eq);
  and and_5 (Slt, Rtype, comparator_6_eq);
  and and_6 (Sltu, Rtype, comparator_7_eq);
  and and_7 (Jr, Rtype, comparator_8_eq);
  or or_1 (NopS, Beq, Jal, J, Jr, Bne);
  Register #(.width(32)) PC_2 (.D(adder_1_out), .Q({Jumper[31:28], PCX}), .clk(CLOCK));  // open: en, clr
  Multiplexer #(.width(5)) multiplexer_3 (
    .in0(Jump[20:16]), .in1(Imm[15:11]), .out(multiplexer_3_out), .sel(RegDst));  // open: en
  Multiplexer #(.width(5)) multiplexer_4 (
    .in0(multiplexer_3_out), .in1({5{1'b1}}), .out(multiplexer_4_out), .sel(Jal));  // open: en
  Multiplexer #(.width(5)) multiplexer_5 (
    .in0(multiplexer_4_out), .in1(Jump[25:21]), .out(multiplexer_5_out), .sel(Swinc));  // open: en
  Comparator #(.width(6)) comparator_11 (.a(Funct), .b({6{1'b0}}), .eq(comparator_11_eq));  // open: gt, lt
  Comparator #(.width(6)) comparator_12 (.a(Funct), .b(6'b000011), .eq(comparator_12_eq));  // open: gt, lt
  Comparator #(.width(6)) comparator_13 (.a(Funct), .b(6'b000010), .eq(comparator_13_eq));  // open: gt, lt
  Comparator #(.width(6)) comparator_14 (.a(Funct), .b(6'b100010), .eq(comparator_14_eq));  // open: gt, lt
  Comparator #(.width(6)) comparator_15 (.a(Funct), .b(6'b100011), .eq(comparator_15_eq));  // open: gt, lt
  Subtractor #(.width(32)) subtractor_1 (.a(adder_2_out), .b(32'h4), .out(subtractor_1_out));  // open: bin, bout
  Multiplexer #(.width(32)) multiplexer_6 (
    .in0(WriteData), .in1({Jumper[31:28], PCX}), .out(multiplexer_6_out), .sel(Jal));  // open: en
  assign bit_extender_1_out = {{16{Imm[15]}}, {Imm, Funct}};  // Bit_Extender bit_extender_1
  assign bit_extender_2_out = {{16{1'b0}}, {Imm, Funct}};  // Bit_Extender bit_extender_2
  and and_8 (Sll, Rtype, comparator_11_eq);
  and and_9 (Sra, Rtype, comparator_12_eq);
  and and_10 (Srl, Rtype, comparator_13_eq);
  and and_11 (Sub, Rtype, comparator_14_eq);
  and and_12 (Subu, Rtype, comparator_15_eq);
  or or_2 (ExtOp, Andi, Ori);
  or or_3 (MemWr, Sw, Swinc);
  or or_4 (nPCsel, Beq, Bne);
  and and_13 (and_13_out, Beq, Eq);
  and and_14 (and_14_out, Bne, Eq);
  or or_5 (Shamt, Sra, Sll, Srl);
  assign ShamtF = {{27{1'b0}}, Imm[10:6]};  // Bit_Extender bit_extender_3
  regfile_main main_1 (
    .Read_Register_1(Jump[25:21]), .Read_Register_2(Jump[20:16]), .Write_Register(multiplexer_5_out),
    .Write_Data(multiplexer_6_out), .Write_Enable(WriteReg), .Clock(CLOCK), .Read_Data_1(Jreg),
    .Read_Data_2(main_1_read_data_2), .s0_Value(s0_Value), .s1_Value(s1_Value), .s2_Value(s2_Value),
    .ra_Value(ra_Value), .sp_Value(sp_Value));
  Multiplexer #(.width(32)) multiplexer_7 (
    .in0(bit_extender_1_out), .in1(bit_extender_2_out), .out(multiplexer_7_out), .sel(ExtOp));  // open: en
  xor xor_1 (branchSign, and_13_out, and_14_out);
  Multiplexer #(.width(32)) multiplexer_8 (
    .in0(adder_1_out), .in1(subtractor_1_out), .out(multiplexer_8_out), .sel(branchSign));  // open: en
  Adder #(.width(32)) adder_2 (.a({Jumper[31:28], PCX}), .b(shifter_1_out), .out(adder_2_out));  // open: cin, cout
  Multiplexer #(.width(32)) multiplexer_9 (.in0(Jreg), .in1(LUI), .out(multiplexer_9_out), .sel(Lui_t));  // open: en
  Multiplexer #(.width(32)) multiplexer_10 (
    .in0(main_1_read_data_2), .in1(multiplexer_7_out), .out(multiplexer_10_out), .sel(ALUSrc));  // open: en
  Shifter #(.width(32)) shifter_1 (.in(multiplexer_7_out), .\dist (5'b00010), .out(shifter_1_out));
  Multiplexer #(.width(32)) multiplexer_11 (
    .in0(multiplexer_9_out), .in1(ShamtF), .out(multiplexer_11_out), .sel(Shamt));  // open: en
  Register #(.width(32)) register_1 (
    .D(multiplexer_12_out), .Q({Opcode, Jump, Imm, Funct}), .clk(CLOCK));  // open: en, clr
  Multiplexer #(.width(32)) multiplexer_12 (
    .in0(INSTRUCTION), .in1({32{1'b0}}), .out(multiplexer_12_out), .sel(NopS));  // open: en
  Multiplexer #(.width(4)) multiplexer_13 (
    .in0(4'b0000), .in1(4'b0001), .out(multiplexer_13_out), .sel(Srl));  // open: en
  Multiplexer #(.width(4)) multiplexer_14 (
    .in0(multiplexer_13_out), .in1(4'b0010), .out(multiplexer_14_out), .sel(Sra));  // open: en
  or or_6 (or_6_out, Add, Addi);
  assign bit_extender_4_out = {{16{1'b0}}, {Imm, Funct}};  // Bit_Extender bit_extender_4
  LED OF (.in(main_2_signed_overflow));
  alu_main main_2 (
    .Switch(ALUCtr), .X(multiplexer_11_out), .Equal(Eq), .Result(main_2_result),
    .Signed_Overflow(main_2_signed_overflow), .Y(multiplexer_10_out));
  Comparator #(.width(6)) comparator_16 (.a(Opcode), .b(6'b001000), .eq(Addi));  // open: gt, lt
  Comparator #(.width(6)) comparator_17 (.a(Opcode), .b(6'b001001), .eq(Addiu));  // open: gt, lt
  Comparator #(.width(6)) comparator_18 (.a(Opcode), .b(6'b001100), .eq(Andi));  // open: gt, lt
  Comparator #(.width(6)) comparator_19 (.a(Opcode), .b(6'b000100), .eq(Beq));  // open: gt, lt
  Comparator #(.width(6)) comparator_20 (.a(Opcode), .b(6'b000101), .eq(Bne));  // open: gt, lt
  Multiplexer #(.width(4)) multiplexer_15 (
    .in0(multiplexer_14_out), .in1(4'b0101), .out(multiplexer_15_out), .sel(or_6_out));  // open: en
  or or_7 (or_7_out, Addu, Addiu);
  Shifter #(.width(32)) shifter_2 (.in(bit_extender_4_out), .\dist (5'b10000), .out(LUI));
  or or_8 (WriteReg, Sltiu, Lw, Andi, Rtype, Lui_t, Jal, Addiu, Addi, Ori, Slti, Swinc);
  Multiplexer #(.width(4)) multiplexer_16 (
    .in0(multiplexer_15_out), .in1(4'b0110), .out(multiplexer_16_out), .sel(or_7_out));  // open: en
  Multiplexer #(.width(4)) multiplexer_17 (
    .in0(multiplexer_16_out), .in1(4'b0111), .out(multiplexer_17_out), .sel(Sub));  // open: en
  Comparator #(.width(6)) comparator_21 (.a(Opcode), .b(6'b001011), .eq(Sltiu));  // open: gt, lt
  Comparator #(.width(6)) comparator_22 (.a(Opcode), .b(6'b001111), .eq(Lui_t));  // open: gt, lt
  Comparator #(.width(6)) comparator_23 (.a(Opcode), .b(6'b100011), .eq(Lw));  // open: gt, lt
  Comparator #(.width(6)) comparator_24 (.a(Opcode), .b(6'b001101), .eq(Ori));  // open: gt, lt
  Multiplexer #(.width(4)) multiplexer_18 (
    .in0(multiplexer_17_out), .in1(4'b1000), .out(multiplexer_18_out), .sel(Subu));  // open: en
  // mem_main main_3: pin names not known; wires that end beside it: main_2_result, main_1_read_data_2, MemWr, CLOCK, main_3_p5
  Multiplexer #(.width(4)) multiplexer_19 (
    .in0(multiplexer_18_out), .in1(4'b1001), .out(multiplexer_19_out), .sel(or_9_out));  // open: en
  or or_9 (or_9_out, And, Andi);
  Multiplexer #(.width(32)) multiplexer_20 (
    .in0(main_2_result), .in1(main_3_p5), .out(WriteData), .sel(Lw));  // open: en
  Multiplexer #(.width(4)) multiplexer_21 (
    .in0(multiplexer_19_out), .in1(4'b1010), .out(multiplexer_21_out), .sel(or_10_out));  // open: en
  or or_10 (or_10_out, Or, Ori);
  Comparator #(.width(6)) comparator_25 (.a(Opcode), .b(6'b001010), .eq(Slti));  // open: gt, lt
  Comparator #(.width(6)) comparator_26 (.a(Opcode), .b(6'b101011), .eq(Sw));  // open: gt, lt
  Comparator #(.width(6)) comparator_27 (.a(Opcode), .b(6'b101100), .eq(Swinc));  // open: gt, lt
  or or_11 (RegDst, Add, Addu, And, Sub, Subu, Sltu, Slt, Sll, Sra, Srl, Or);
  Multiplexer #(.width(4)) multiplexer_22 (
    .in0(multiplexer_21_out), .in1(4'b1011), .out(multiplexer_22_out), .sel(or_13_out));  // open: en
  or or_12 (or_12_out, Sltu, Sltiu);
  or or_13 (or_13_out, Slti, Slt);
  or or_14 (ALUSrc, Lw, Addiu, Addi, Andi, Swinc, Ori, Sltiu, Slti, Sw);
  Multiplexer #(.width(4)) multiplexer_23 (
    .in0(multiplexer_22_out), .in1(4'b1100), .out(ALUCtr), .sel(or_12_out));  // open: en
  // Probe on ALUCtr
  // Probe on ALUSrc
  // Probe on WriteReg
  // Probe on MemWr
  // Probe on Beq
  // Probe on ExtOp
  // Probe on Bne
  // Probe on Lui_t
  // Probe on Jal
  // Probe on Jr
  // Probe on nPCsel
  // Probe on Shamt
  // Probe on Swinc
  // Probe on NopS
  // Probe on branchSign
  // Probe on RegDst
  // Probe on Lw

  // Other names for the same wires on the sheet: Imm[5:0] = Funct; Jump[15:0] = {Imm, Funct};
  //   Jumper[27:2] = {Jump, Imm, Funct}; ShamtI[4:0] = Imm[10:6]; Rd[4:0] = Imm[15:11]; Rt[4:0] = Jump[20:16];
  //   Rs[4:0] = Jump[25:21]; clk = CLOCK; fetch_addr[31:0] = FETCH_ADDRESS; PC[31:0] = FETCH_ADDRESS; MemToReg = Lw;
  //   PCX[31:28] = Jumper[31:28]; ra[31:0] = ra_Value; s0[31:0] = s0_Value; s1[31:0] = s1_Value; s2[31:0] = s2_Value;
  //   sp[31:0] = sp_Value

  // Notes on the sheet:
  //   Output
  //   J Type
  //   These are outputs/inputs from run.circ
  //   Rtype
  //   Inputs
  //   PC+4
  //   CONTROL!!!
  //   These are DEBUG/TEST outputs from your circuit.
  //   I-Type
  //   Instruction
  //   Write data in RegFile
endmodule
