// Logisim project regfile.circ as structural Verilog: 1 circuit, main circuit main
module main (
  input  [4:0] Read_Register_1,
  input  [4:0] Read_Register_2,
  input  [4:0] Write_Register,
  input  [31:0] Write_Data,
  input  Write_Enable,
  input  Clock,
  output [31:0] s0_Value,
  output [31:0] s1_Value,
  output [31:0] s2_Value,
  output [31:0] ra_Value,
  output [31:0] sp_Value,
  output [31:0] Read_Data_1,
  output [31:0] Read_Data_2
);

  wire _0, _1, _2, _3, _4, _5, _6, _7, _8, _9, _10, _11, _12, _13, _14, _15, _16, _17, _18, _19, _20, _21,
       _22, _23, _24, _25, _26, _27, _28, _29, _30, _31;
  wire [31:0] r0, r1, r2, r3, r4, r5, r6, r7, r8, r9, r10, r11, r12, r13, r14, r15, r19, r20, r21, r22, r23,
       r24, r25, r26, r27, r28, r30, undriven;

  Demultiplexer #(.select(5)) demultiplexer_1 (
    .out0(_0), .out1(_1), .out2(_2), .out3(_3), .out4(_4), .out5(_5), .out6(_6), .out7(_7), .out8(_8),
    .out9(_9), .out10(_10), .out11(_11), .out12(_12), .out13(_13), .out14(_14), .out15(_15), .out16(_16),
    .out17(_17), .out18(_18), .out19(_19), .out20(_20), .out21(_21), .out22(_22), .out23(_23), .out24(_24),
    .out25(_25), .out26(_26), .out27(_27), .out28(_28), .out29(_29), .out30(_30), .out31(_31),
    .in(Write_Enable), .sel(Write_Register));  // open: en
  Register #(.width(32)) register_1 (.en(_0), .Q(r0), .clk(Clock));  // open: D, clr
  Register #(.width(32)) register_2 (.D(Write_Data), .en(_10), .Q(r10), .clk(Clock));  // open: clr
  Register #(.width(32)) register_3 (.D(Write_Data), .en(_11), .Q(r11), .clk(Clock));  // open: clr
  Register #(.width(32)) register_4 (.D(Write_Data), .en(_12), .Q(r12), .clk(Clock));  // open: clr
  Register #(.width(32)) register_5 (.D(Write_Data), .en(_13), .Q(r13), .clk(Clock));  // open: clr
  Register #(.width(32)) register_6 (.D(Write_Data), .en(_14), .Q(r14), .clk(Clock));  // open: clr
  Register #(.width(32)) register_7 (.D(Write_Data), .en(_15), .Q(r15), .clk(Clock));  // open: clr
  Register #(.width(32)) register_8 (.D(Write_Data), .en(_16), .Q(s0_Value), .clk(Clock));  // open: clr
  Register #(.width(32)) register_9 (.D(Write_Data), .en(_17), .Q(s1_Value), .clk(Clock));  // open: clr
  Register #(.width(32)) register_10 (.D(Write_Data), .en(_18), .Q(s2_Value), .clk(Clock));  // open: clr
  Register #(.width(32)) register_11 (.D(Write_Data), .en(_19), .Q(r19), .clk(Clock));  // open: clr
  Register #(.width(32)) register_12 (.D(Write_Data), .en(_1), .Q(r1), .clk(Clock));  // open: clr
  Register #(.width(32)) register_13 (.D(Write_Data), .en(_2), .Q(r2), .clk(Clock));  // open: clr
  Register #(.width(32)) register_14 (.D(Write_Data), .en(_3), .Q(r3), .clk(Clock));  // open: clr
  Register #(.width(32)) register_15 (.D(Write_Data), .en(_4), .Q(r4), .clk(Clock));  // open: clr
  Register #(.width(32)) register_16 (.D(Write_Data), .en(_5), .Q(r5), .clk(Clock));  // open: clr
  Register #(.width(32)) register_17 (.D(Write_Data), .en(_6), .Q(r6), .clk(Clock));  // open: clr
  Register #(.width(32)) register_18 (.D(Write_Data), .en(_7), .Q(r7), .clk(Clock));  // open: clr
  Register #(.width(32)) register_19 (.D(Write_Data), .en(_8), .Q(r8), .clk(Clock));  // open: clr
  Register #(.width(32)) register_20 (.D(Write_Data), .en(_9), .Q(r9), .clk(Clock));  // open: clr
  Register #(.width(32)) register_21 (.D(Write_Data), .en(_21), .Q(r21), .clk(Clock));  // open: clr
  Register #(.width(32)) register_22 (.D(Write_Data), .en(_20), .Q(r20), .clk(Clock));  // open: clr
  Register #(.width(32)) register_23 (.D(Write_Data), .en(_22), .Q(r22), .clk(Clock));  // open: clr
  Register #(.width(32)) register_24 (.D(Write_Data), .en(_23), .Q(r23), .clk(Clock));  // open: clr
  Register #(.width(32)) register_25 (.D(Write_Data), .en(_24), .Q(r24), .clk(Clock));  // open: clr
  Register #(.width(32)) register_26 (.D(Write_Data), .en(_25), .Q(r25), .clk(Clock));  // open: clr
  Register #(.width(32)) register_27 (.D(Write_Data), .en(_26), .Q(r26), .clk(Clock));  // open: clr
  Register #(.width(32)) register_28 (.D(Write_Data), .en(_27), .Q(r27), .clk(Clock));  // open: clr
  Register #(.width(32)) register_29 (.D(Write_Data), .en(_28), .Q(r28), .clk(Clock));  // open: clr
  Register #(.width(32)) register_30 (.D(Write_Data), .en(_29), .Q(sp_Value), .clk(Clock));  // open: clr
  Register #(.width(32)) register_31 (.D(Write_Data), .en(_30), .Q(r30), .clk(Clock));  // open: clr
  Register #(.width(32)) register_32 (.D(Write_Data), .en(_31), .Q(ra_Value), .clk(Clock));  // open: clr
  Multiplexer #(.select(5), .width(32)) multiplexer_1 (
    .in0(r0), .in1(r1), .in2(r2), .in3(r3), .in4(r4), .in5(r5), .in6(r6), .in7(r7), .in8(r8), .in9(r9),
    .in10(r10), .in11(r11), .in12(r12), .in13(r13), .in14(r14), .in15(r15), .in16(s0_Value), .in17(s1_Value),
    .in18(s2_Value), .in19(r19), .in20(r20), .in21(r21), .in22(r22), .in23(r23), .in24(r24), .in25(r25),
    .in26(r26), .in27(r27), .in28(r28), .in29(sp_Value), .in30(r30), .in31(ra_Value), .out(Read_Data_1),
    .sel(Read_Register_1));  // open: en
  Multiplexer #(.select(5), .width(32)) multiplexer_2 (
    .in0(r0), .in1(r1), .in2(r2), .in3(undriven), .in4(r4), .in5(r5), .in6(r6), .in7(r7), .in8(r8), .in9(r9),
    .in10(r10), .in11(r11), .in12(r12), .in13(r13), .in14(r14), .in15(r15), .in16(s0_Value), .in17(s1_Value),
    .in18(s2_Value), .in19(r19), .in20(r20), .in21(r21), .in22(r22), .in23(r23), .in24(r24), .in25(r25),
    .in26(r26), .in27(r27), .in28(r28), .in29(sp_Value), .in30(r30), .in31(ra_Value), .out(Read_Data_2),
    .sel(Read_Register_2));  // open: en

  // Other names for the same wires on the sheet: clk = Clock; r31[31:0] = ra_Value; ra[31:0] = ra_Value;
  //   read_data1[31:0] = Read_Data_1; read_data2[31:0] = Read_Data_2; read_reg1[4:0] = Read_Register_1;
  //   read_reg2[4:0] = Read_Register_2; r16[31:0] = s0_Value; s0[31:0] = s0_Value; r17[31:0] = s1_Value;
  //   s1[31:0] = s1_Value; r18[31:0] = s2_Value; s2[31:0] = s2_Value; r29[31:0] = sp_Value; sp[31:0] = sp_Value;
  //   write_en = Write_Enable; write_reg[4:0] = Write_Register

  // Notes on the sheet:
  //   INPUTS to your circuit
  //   DON'T CHANGE THE LOCATIONS OF THE INPUTS AND OUTPUTS!
  //   These are DEBUG/TEST outputs from your circuit.
  //   OUTPUTS from your circuit
endmodule
